// Logisim project 51cpu.circ as structural Verilog: 4 circuits, main circuit main
module main (
  input  [1:0] in_1,
  input  [2:0] in_2,
  input  in_3
);

  wire button_1_out, CLK, clock_1_out, CLR, counter_1_q, P0LE, P0OE, P0PORTOE, SFR_ALE, SFR_AOE, SFR_BLE,
       SFR_BOE, SFR_SPLE, SFR_SPOE;
  wire [7:0] P0_out, P0_port_out, pull_resistor_1_node, register_1_q, register_2_q, register_3_q, undriven;
  wire [7:7] rom_1_data;

  Button button_1 (.out(button_1_out));
  Clock clock_1 (.out(clock_1_out));
  Counter #(.width(1), .max('h1)) counter_1 (
    .load(1'b1), .D(1'b1), .count(1'b1), .Q(counter_1_q), .clk(clock_1_out), .clr(1'b0));  // open: carry
  Multiplexer #(.select(3)) multiplexer_1 (
    .in0(button_1_out), .in1(clock_1_out), .in2(counter_1_q), .out(CLK), .sel(in_2), .en(1'b1));  // open: in3, in4, in5, in6, in7
  Button button_2 (.out(CLR));
  Pull_Resistor pull_resistor_1 (.node(pull_resistor_1_node));
  P0 P0 (
    .IN(pull_resistor_1_node), .LE(P0LE), .CLK(CLK), .CLR(CLR), .in_5(undriven), .OUT(P0_out),
    .PORT_OUT(P0_port_out));
  assign pull_resistor_1_node = P0OE ? P0_out : 8'bz;  // Controlled_Buffer controlled_buffer_1
  assign pull_resistor_1_node = P0PORTOE ? P0_port_out : 8'bz;  // Controlled_Buffer controlled_buffer_2
  assign pull_resistor_1_node = SFR_AOE ? register_1_q : 8'bz;  // Controlled_Buffer controlled_buffer_3
  // Probe on register_1_q
  Register register_1 (.D(pull_resistor_1_node), .en(SFR_ALE), .Q(register_1_q), .clk(CLK), .clr(CLR));
  // Probe on pull_resistor_1_node
  assign pull_resistor_1_node = SFR_BOE ? register_2_q : 8'bz;  // Controlled_Buffer controlled_buffer_4
  // Probe on register_2_q
  Register register_2 (.D(pull_resistor_1_node), .en(SFR_BLE), .Q(register_2_q), .clk(CLK), .clr(CLR));
  Register register_3 (.D(pull_resistor_1_node), .en(SFR_SPLE), .Q(register_3_q), .clk(CLK), .clr(CLR));
  assign pull_resistor_1_node = SFR_SPOE ? register_3_q : 8'bz;  // Controlled_Buffer controlled_buffer_5
  // Probe on register_3_q
  ROM #(.addrWidth(2)) rom_1 (
    .addr(in_1), .data({rom_1_data[7], P0PORTOE, P0OE, P0LE, SFR_BLE, SFR_BOE, SFR_ALE, SFR_AOE}), .sel(in_3));

  // Notes on the sheet:
  //   contents of rom_1 (hex, n*v repeats v):
  //   4*1
endmodule

module SREG (
  input  [1:0] S1_0,
  input  CLK,
  input  CLR,
  input  [7:0] IN,
  output [7:0] OUT
);

  wire [7:0] multiplexer_1_out, shifter_1_out, shifter_2_out;

  Shifter #(.shift("lr")) shifter_1 (.in(OUT), .\dist (3'b001), .out(shifter_1_out));
  Shifter shifter_2 (.in(OUT), .\dist (3'b001), .out(shifter_2_out));
  Multiplexer #(.select(2), .width(8)) multiplexer_1 (
    .in0(OUT), .in1(shifter_1_out), .in2(shifter_2_out), .in3(IN), .out(multiplexer_1_out), .sel(S1_0),
    .en(1'b1));
  Register register_1 (.D(multiplexer_1_out), .en(1'b1), .Q(OUT), .clk(CLK), .clr(CLR));
endmodule

module P0 (
  input  [7:0] IN,
  input  LE,
  input  CLK,
  input  CLR,
  input  [7:0] in_5,
  output [7:0] OUT,
  output [7:0] PORT_OUT
);

  Register register_1 (.D(IN), .en(LE), .Q(OUT), .clk(CLK), .clr(CLR));
  assign in_5 = OUT;  // Buffer buffer_1, 8 bits wide

  assign PORT_OUT = in_5;

  // Notes on the sheet:
  //   buffer_1 drives only 0 and floats otherwise
endmodule

module RAM (
  input  [7:0] in_1,
  input  [7:0] in_2,
  input  in_3,
  input  in_4,
  input  in_5,
  input  [7:0] in_6,
  input  in_7,
  output [7:0] out_8
);

  wire not_1_out;

  not not_1 (not_1_out, in_1[7]);
  assign out_8 = in_7 ? in_6 : 8'bz;  // Controlled_Buffer controlled_buffer_1
  RAM_part #(.addrWidth(7), .bus("separate")) ram_1 (
    .addr(in_1[6:0]), .din(in_2), .data(out_8), .str(in_3), .sel(not_1_out), .clk(in_4), .ld(in_5), .clr(1'b0));
endmodule
